// Logisim project lab2.circ as structural Verilog: 2 circuits, main circuit main
module main (
  input  in_1,
  input  in_2,
  input  in_3,
  input  in_4,
  input  in_5,
  input  in_6,
  input  in_7,
  input  in_8,
  output out_9,
  output out_10,
  output out_11,
  output out_12
);

  wire and_1_out, and_2_out, and_3_out, and_4_out, and_5_out, and_6_out, and_7_out, and_8_out, and_9_out,
       and_10_out, and_11_out, and_12_out, \d_триггер_1_out_3 , \d_триггер_2_out_3 , \d_триггер_3_out_3 ,
       \d_триггер_4_out_3 , \d_триггер_5_out_3 , \d_триггер_6_out_3 , \d_триггер_7_out_3 ,
       \d_триггер_8_out_3 , not_1_out, not_2_out, or_1_out, or_2_out, or_3_out, or_4_out;

  not not_1 (not_1_out, in_5);
  and and_1 (and_1_out, in_6, not_2_out);
  not not_2 (not_2_out, in_7);
  \D_триггер  \d_триггер_1  (.in_1(in_4), .in_2(and_2_out), .out_3(\d_триггер_1_out_3 ));
  and and_2 (and_2_out, and_1_out, not_1_out);
  \D_триггер  \d_триггер_2  (.in_1(in_4), .in_2(and_3_out), .out_3(\d_триггер_2_out_3 ));
  and and_3 (and_3_out, and_1_out, in_5);
  and and_4 (and_4_out, in_6, in_7, in_8);
  and and_5 (and_5_out, not_1_out, \d_триггер_1_out_3 );
  and and_6 (and_6_out, in_5, \d_триггер_2_out_3 );
  or or_1 (or_1_out, and_6_out, and_5_out);
  \D_триггер  \d_триггер_3  (.in_1(in_3), .in_2(and_2_out), .out_3(\d_триггер_3_out_3 ));
  and and_7 (and_7_out, not_1_out, \d_триггер_3_out_3 );
  \D_триггер  \d_триггер_4  (.in_1(in_3), .in_2(and_3_out), .out_3(\d_триггер_4_out_3 ));
  and and_8 (and_8_out, in_5, \d_триггер_4_out_3 );
  \D_триггер  \d_триггер_5  (.in_1(in_2), .in_2(and_2_out), .out_3(\d_триггер_5_out_3 ));
  \D_триггер  \d_триггер_6  (.in_1(in_2), .in_2(and_3_out), .out_3(\d_триггер_6_out_3 ));
  or or_2 (or_2_out, and_8_out, and_7_out);
  and and_9 (and_9_out, not_1_out, \d_триггер_5_out_3 );
  and and_10 (and_10_out, in_5, \d_триггер_6_out_3 );
  or or_3 (or_3_out, and_10_out, and_9_out);
  \D_триггер  \d_триггер_7  (.in_1(in_1), .in_2(and_2_out), .out_3(\d_триггер_7_out_3 ));
  and and_11 (and_11_out, not_1_out, \d_триггер_7_out_3 );
  \D_триггер  \d_триггер_8  (.in_1(in_1), .in_2(and_3_out), .out_3(\d_триггер_8_out_3 ));
  and and_12 (and_12_out, in_5, \d_триггер_8_out_3 );
  or or_4 (or_4_out, and_12_out, and_11_out);
  assign out_9 = and_4_out ? or_4_out : 1'bz;  // Controlled_Buffer controlled_buffer_1
  assign out_10 = and_4_out ? or_3_out : 1'bz;  // Controlled_Buffer controlled_buffer_2
  assign out_11 = and_4_out ? or_2_out : 1'bz;  // Controlled_Buffer controlled_buffer_3
  assign out_12 = and_4_out ? or_1_out : 1'bz;  // Controlled_Buffer controlled_buffer_4
endmodule

module \D_триггер  (
  input  in_1,
  input  in_2,
  output out_3
);

  wire and_1_out, and_2_out, nor_1_out, not_1_out;

  not not_1 (not_1_out, in_1);
  and and_1 (and_1_out, in_1, in_2);
  and and_2 (and_2_out, in_2, not_1_out);
  nor nor_1 (nor_1_out, and_1_out, out_3);
  nor nor_2 (out_3, nor_1_out, and_2_out);
endmodule
